# Fritzing sketch Pakan & Minum (Schematic) (saved by Fritzing 0.9.3b)

parts:
  M1 = DOIT Esp32 DevKit v1 (30 pins long, 11 pins width) [part_number=ESP32S-PIN30]
  Part1 = Adafruit DS3231 [part_number="Adafruit #3013"]
  L298N1 = L298N DC motor driver
  M2 = DC Motor  # not connected
  M3 = DC Motor  # not connected
  TCS1 = TCS3200
  L298N2 = L298N DC motor driver
  M4 = DC Motor  # not connected
  VCC1 = Battery
  J1 = Basic Servo
  S1 = Round Pushbutton  # not connected
  LED1 = LED - 5mm [color="Red (633nm)" package="5 mm [THT]"]

nets:
  3V3: M1.3V3, J1.vcc
  GND: M1.GND, Part1.GND, L298N1.GND, VCC1.-
  N1: M1.D4, TCS1.S0
  N2: M1.RX2, TCS1.S1
  N3: M1.TX2, TCS1.S2
  N4: M1.D5, TCS1.S3
  N5: M1.D18, LED1.anode
  N6: M1.D21, Part1.SDA
  N7: M1.D22, Part1.SCL
  N8: M1.D34, L298N1.IN4
  N9: M1.D35, L298N1.IN3
  N10: M1.D32, L298N1.IN2
  N11: M1.D33, L298N1.IN1
  N12: M1.D27, L298N2.IN1
  N13: M1.D14, L298N2.IN2
  N14: M1.D13, J1.pulse
  VIN: M1.VIN, Part1.Vin
  N15: L298N1.12V, VCC1.+

custom parts:
  DOIT Esp32 DevKit v1 (30 pins long, 11 pins width): The DOIT Esp32 DevKit v1 is one of the development board created by DOIT to evaluate the ESP-WROOM-32 module. It is based on the ESP32 microcontroller that boasts Wifi, Bluetooth, Ethernet and Low Power support all in a single chip. (vanepp) made breadboard work, adjusted pin numbering and labels and reduced size of schematic and cleaned up pcb. This chip is 30pins long (2 x15) and 11 pins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
  Adafruit DS3231: The datasheet for the DS3231 explains that this part is an "Extremely Accurate I²C-Integrated RTC/TCXO/Crystal". And, hey, it does exactly what it says on the tin! This Real Time Clock (RTC) is the most precise you can get in a small, low power package. Most RTCs use an external 32kHz timing crystal that is used to keep time with low current draw. And that's all well and good, but those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
  L298N DC motor driver: 2x DC motor driver with 78M05 positive voltage regulator (7..35 V) L298N: max 46 V, 2 A Set 5 V Enable jumper to enable 5 V regultor (needed for the L298N) and +5 V output at screw terminal or supply external +5 V at screw terminal Set ENA and/or ENB to +5 V to enable motor permanently or supply ENA and/or ENB with PWM signal IN1 and IN2 set rotation directory for motor A (OUT1/OUT2) IN2 and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
  TCS3200: COLOR SENSING TCS3200
